# Fritzing sketch Esquematico (saved by Fritzing 0.7.1b)

parts:
  Parte3 = IMU Digital Combo Board 6DOF
  Arduino2 = Arduino
  Parte4 = Logic Level Converter

nets:
  3.3V: Parte3.3.3V, Arduino2.3V3, Parte4.LV
  GND: Parte3.GND, Arduino2.GND, Parte4.GND
  N1: Parte3.SDA, Parte4.TX2_LV
  N2: Parte3.SCL, Parte4.TX_LV
  N3: Arduino2.+5V, Parte4.HV
  N4: Arduino2.A4, Parte4.TX_HV
  N5: Arduino2.A5, Parte4.TX2_HV
